// Logisim project 4_bit_alu.circ as structural Verilog: 2 circuits, main circuit main
module main (
  input  [1:0] operation,
  input  a_invert,
  input  b_invert,
  input  c_in,
  input  [3:0] a,
  input  [3:0] b,
  output [3:0] result,
  output c_out
);

  wire alu_1_bit_1_c_out, alu_1_bit_2_c_out, alu_1_bit_3_c_out;

  alu_1_bit alu_1_bit_1 (
    .a(a[0]), .b(b[0]), .a_invert(a_invert), .b_invert(b_invert), .c_in(c_in), .operation(operation),
    .c_out(alu_1_bit_1_c_out), .result(result[0]));
  alu_1_bit alu_1_bit_2 (
    .a(a[1]), .b(b[1]), .a_invert(a_invert), .b_invert(b_invert), .c_in(alu_1_bit_1_c_out),
    .operation(operation), .c_out(alu_1_bit_2_c_out), .result(result[1]));
  alu_1_bit alu_1_bit_3 (
    .a(a[2]), .b(b[2]), .a_invert(a_invert), .b_invert(b_invert), .c_in(alu_1_bit_2_c_out),
    .operation(operation), .c_out(alu_1_bit_3_c_out), .result(result[2]));
  alu_1_bit alu_1_bit_4 (
    .a(a[3]), .b(b[3]), .a_invert(a_invert), .b_invert(b_invert), .c_in(alu_1_bit_3_c_out),
    .operation(operation), .c_out(c_out), .result(result[3]));
endmodule

module alu_1_bit (
  input  a_invert,
  input  b_invert,
  input  c_in,
  input  [1:0] operation,
  input  a,
  input  b,
  output result,
  output c_out
);

  wire adder_1_out, and_1_out, multiplexer_1_out, multiplexer_2_out, not_1_out, not_2_out, or_1_out;

  not not_1 (not_1_out, a);
  Multiplexer #(.enable("false")) multiplexer_1 (.in0(a), .in1(not_1_out), .out(multiplexer_1_out), .sel(a_invert));
  not not_2 (not_2_out, b);
  Multiplexer #(.enable("false")) multiplexer_2 (.in0(b), .in1(not_2_out), .out(multiplexer_2_out), .sel(b_invert));
  and and_1 (and_1_out, multiplexer_1_out, multiplexer_2_out);
  or or_1 (or_1_out, multiplexer_1_out, multiplexer_2_out);
  Adder #(.width(1)) adder_1 (
    .a(multiplexer_1_out), .b(multiplexer_2_out), .out(adder_1_out), .cin(c_in), .cout(c_out));
  Multiplexer #(.enable("false"), .select(2)) multiplexer_3 (
    .in0(and_1_out), .in1(or_1_out), .in2(adder_1_out), .in3(1'b0), .out(result), .sel(operation));
endmodule
